// Logisim project meiasoma.circ as structural Verilog: 2 circuits, main circuit main
module main (
  input  A,
  input  B,
  output S,
  output Cout
);

  and and_1 (Cout, A, B);
  xor xor_1 (S, A, B);
endmodule

module completo (
  input  Cin,
  input  A0,
  input  A1,
  input  A2,
  input  A3,
  input  B0,
  input  B1,
  input  B2,
  input  B3,
  output S0,
  output S1,
  output S2,
  output S3,
  output OVERFLOW
);

  wire main_1_cout, main_2_cout, main_3_cout, main_4_cout;

  main main_1 (.A(A0), .B(B0), .Cout(main_1_cout), .S(S0));
  main main_2 (.A(A1), .B(B1), .Cout(main_2_cout), .S(S1));
  main main_3 (.A(A2), .B(B2), .Cout(main_3_cout), .S(S2));
  main main_4 (.A(A3), .B(B3), .Cout(main_4_cout), .S(S3));
  xor xor_1 (OVERFLOW, main_3_cout, main_4_cout);
endmodule
