// Logisim project somador_completo.circ as structural Verilog: 2 circuits, main circuit main
module main (
  input  Vin,
  input  A,
  input  B,
  output S,
  output Vout
);

  Somador_completo somador_completo_1 (.A(A), .B(B), .Vin(Vin), .Vout(Vout), .S(S));
endmodule

module Somador_completo (
  input  Vin,
  input  A,
  input  B,
  output S,
  output Vout
);

  wire and_1_out, and_2_out, and_3_out, xor_1_out;

  xor xor_1 (xor_1_out, A, B);
  and and_1 (and_1_out, A, Vin);
  and and_2 (and_2_out, A, B);
  and and_3 (and_3_out, B, Vin);
  or or_1 (Vout, and_1_out, and_2_out, and_3_out);
  xor xor_2 (S, xor_1_out, Vin);
endmodule
